// Logisim project Processor.circ as structural Verilog: 3 circuits, main circuit main
module main (
  input  in_1,
  output Cout
);

  wire and_1_out, clock_1_out, control_unit_1_alu_source, control_unit_1_bin, control_unit_1_branch,
       control_unit_1_jump, control_unit_1_memory_read, control_unit_1_memory_write,
       control_unit_1_reg_write, main_1_equal;
  wire [1:0] control_unit_1_alu_op;
  wire [3:0] bit_extender_3_out;
  wire [6:0] rom_1_data;
  wire [9:0] adder_1_out, bit_extender_2_out, bit_extender_4_out, multiplexer_1_out, multiplexer_2_out,
       register_1_q;
  wire [9:7] rom_1_data_2;
  wire [15:0] bit_extender_5_out, main_1_res, multiplexer_3_out, multiplexer_4_out, ram_1_data,
       register_file_1_read_data1, register_file_1_read_data_2;

  Register #(.width(10)) register_1 (
    .D(multiplexer_2_out), .Q(register_1_q), .clk(clock_1_out), .clr(in_1));  // open: en
  Clock clock_1 (.out(clock_1_out));
  Adder #(.width(10)) adder_1 (.a(10'h1), .b(register_1_q), .out(adder_1_out));  // open: cin, cout
  Bit_Extender #(.in_width(7), .out_width(10)) bit_extender_1 ();  // open: in, out
  ROM #(.addrWidth(10), .dataWidth(10)) rom_1 (.addr(register_1_q), .data({rom_1_data_2, rom_1_data}));  // open: sel
  assign bit_extender_2_out = {{3{1'b0}}, rom_1_data};  // Bit_Extender bit_extender_2
  assign bit_extender_3_out = {{3{1'b0}}, rom_1_data[0]};  // Bit_Extender bit_extender_3
  Control_Unit control_unit_1 (
    .Opcode(rom_1_data_2), .ALU_op(control_unit_1_alu_op), .Jump(control_unit_1_jump),
    .Reg_Write(control_unit_1_reg_write), .Memory_Write(control_unit_1_memory_write),
    .ALU_Source(control_unit_1_alu_source), .Branch(control_unit_1_branch),
    .Memory_Read(control_unit_1_memory_read), .Bin(control_unit_1_bin));
  Multiplexer #(.width(10)) multiplexer_1 (
    .in0(adder_1_out), .in1(bit_extender_2_out), .out(multiplexer_1_out), .sel(control_unit_1_jump));  // open: en
  assign bit_extender_4_out = {{7{1'b0}}, rom_1_data[2:0]};  // Bit_Extender bit_extender_4
  Multiplexer #(.width(10)) multiplexer_2 (
    .in0(multiplexer_1_out), .in1(bit_extender_4_out), .out(multiplexer_2_out), .sel(and_1_out));  // open: en
  Register_File register_file_1 (
    .Read_Data1(register_file_1_read_data1), .Read_Data_2(register_file_1_read_data_2),
    .Write_Data(multiplexer_3_out), .Write_on_Registor(rom_1_data[2:1]), .Write(clock_1_out),
    .Clock_Pulse(control_unit_1_reg_write), .Read_Register_1(rom_1_data[6:5]),
    .Read_Register_2(rom_1_data[4:3]));
  assign bit_extender_5_out = {{6{1'b0}}, bit_extender_4_out};  // Bit_Extender bit_extender_5
  Multiplexer #(.width(16)) multiplexer_3 (
    .in0(main_1_res), .in1(ram_1_data), .out(multiplexer_3_out), .en(control_unit_1_memory_read));  // open: sel
  Multiplexer #(.width(16)) multiplexer_4 (
    .in0(register_file_1_read_data_2), .in1(bit_extender_5_out), .out(multiplexer_4_out),
    .sel(control_unit_1_alu_source));  // open: en
  ALU_main main_1 (
    .Cin(control_unit_1_bin), .A(register_file_1_read_data1), .B(multiplexer_4_out),
    .Bin(control_unit_1_bin), .Dst(bit_extender_3_out), .equal(main_1_equal), .s1s0(control_unit_1_alu_op),
    .res(main_1_res), .cout(Cout));
  and and_1 (and_1_out, control_unit_1_branch, main_1_equal);
  RAM #(.addrWidth(16), .dataWidth(16), .bus("separate")) ram_1 (
    .addr(main_1_res), .din(register_file_1_read_data_2), .data(ram_1_data),
    .str(control_unit_1_memory_write), .ld(control_unit_1_memory_read));  // open: sel, clk, clr
endmodule

module Register_File (
  input  [15:0] Write_Data,
  input  [1:0] Read_Register_1,
  input  [1:0] Write_on_Registor,
  input  [1:0] Read_Register_2,
  input  Write,
  input  Clock_Pulse,
  output [15:0] Read_Data1,
  output [15:0] Read_Data_2
);

  wire and_1_out, and_2_out, and_3_out, and_4_out, decoder_1_out0, decoder_1_out1, decoder_1_out2;
  wire [15:0] register_1_q, register_2_q, register_3_q, register_4_q;

  Decoder #(.select(2)) decoder_1 (
    .out0(decoder_1_out0), .out1(decoder_1_out1), .out2(decoder_1_out2), .sel(Write_on_Registor));  // open: out3, en
  and and_1 (and_1_out, decoder_1_out0, Write);
  and and_2 (and_2_out, decoder_1_out1, Write);
  and and_3 (and_3_out, decoder_1_out2, Write);
  and and_4 (and_4_out, decoder_1_out2, Write);
  Register #(.width(16)) register_1 (.D(Write_Data), .en(and_1_out), .Q(register_1_q), .clk(Clock_Pulse));  // open: clr
  Register #(.width(16)) register_2 (.D(Write_Data), .en(and_2_out), .Q(register_2_q), .clk(Clock_Pulse));  // open: clr
  Register #(.width(16)) register_3 (.D(Write_Data), .en(and_3_out), .Q(register_3_q), .clk(Clock_Pulse));  // open: clr
  Register #(.width(16)) register_4 (.D(Write_Data), .en(and_4_out), .Q(register_4_q), .clk(Clock_Pulse));  // open: clr
  Multiplexer #(.select(2), .width(16)) multiplexer_1 (
    .in0(register_1_q), .in1(register_2_q), .in2(register_3_q), .in3(register_4_q), .out(Read_Data1),
    .sel(Read_Register_1));  // open: en
  Multiplexer #(.select(2), .width(16)) multiplexer_2 (
    .in0(register_1_q), .in1(register_2_q), .in2(register_4_q), .in3(register_4_q), .out(Read_Data_2),
    .sel(Read_Register_2));  // open: en
endmodule

module Control_Unit (
  input  [2:0] Opcode,
  output [1:0] ALU_op,
  output Jump,
  output Reg_Write,
  output Memory_Write,
  output ALU_Source,
  output Branch,
  output Memory_Read,
  output Bin
);

  wire decoder_1_out0, decoder_1_out2, decoder_1_out3, or_1_out;

  Decoder #(.select(3)) decoder_1 (
    .out0(decoder_1_out0), .out1(Bin), .out2(decoder_1_out2), .out3(decoder_1_out3), .out4(Memory_Read),
    .out5(Memory_Write), .out6(Branch), .out7(Jump), .sel(Opcode));  // open: en
  Multiplexer #(.width(2)) multiplexer_1 (.in0(2'b00), .in1(Opcode[2:1]), .out(ALU_op), .sel(or_1_out));  // open: en
  or or_1 (or_1_out, decoder_1_out0, Bin, decoder_1_out2, decoder_1_out3);
  or or_2 (Reg_Write, Memory_Read, decoder_1_out0, Bin, decoder_1_out2, decoder_1_out3);
  or or_3 (ALU_Source, decoder_1_out0, Bin);
endmodule
